# Fritzing sketch huzzah_adc_temp (saved by Fritzing 0.9.2b)
circuit board: 7cm x 5cm
breadboards: 2

parts:
  DS1 = DS18B20 1-Wire Temperature Sensor [part_number=DS18B20]  # not connected
  C1 = Ceramic Capacitor [capacitance=0.1µF package="100 mil [THT, multilayer]"]
  R2 = Resistor [tolerance=±5% resistance=150 package=THT]
  R3 = Resistor [tolerance=±5% resistance=150 package=THT]
  R4 = Resistor [tolerance=±5% resistance=150 package=THT]
  U1 = Voltage Regulator - Variable [package="TO220 [THT]"]
  R1 = Resistor [tolerance=±5% resistance=150 package=THT]
  JACK1 = 2.1mm DC Barrel Jack
  U2 = MCP3008 [package="DIP16 [THT]"]
  Composant1 = HUZZAH ESP8266 Breakout
  C2 = Electrolytic Capacitor [capacitance=10µF package="100 mil [THT, electrolytic]"]

nets:
  N1: C1.0, R1.Pin_1, JACK1.sleeve, U2.DGND, U2.AGND, Composant1.GND, C2.-
  N2: C1.1, U1.IN, JACK1.center
  VCC: R2.Pin_0, U1.OUT, U2.Vref, U2.VCC, Composant1.VIN, C2.+
  N3: R2.Pin_1, R3.Pin_1
  N4: R3.Pin_0, R4.Pin_0
  N5: R4.Pin_1, U1.ADJ, R1.Pin_0
  N6: U2.CS/SHDN, Composant1.GPIO15
  N7: U2.Din, Composant1.GPIO13
  N8: U2.Dout, Composant1.GPIO12
  N9: U2.CLK, Composant1.GPIO14

custom parts:
  2.1mm DC Barrel Jack: 2.1mm DC Barrel Jack with Thru-Hole Connectors (breadboardable)
  MCP3008: 8 Channels 10-Bit ADC with SPI interface
  HUZZAH ESP8266 Breakout: The ESP8266 processor from Espressif is an 80 MHz microcontroller with a full WiFi front-end (both as client and access point) and TCP/IP stack with DNS support as well.
